# Fritzing sketch ferrarisCounterESP_schematic (saved by Fritzing 0.9.3b)
circuit board: 5.23974cm x 5.21494cm
breadboards: 1

parts:
  U1 = NodeMCU V1.0
  0_96"_OLED = Grove OLED 128x96
  R2 = Resistor [tolerance=±5% resistance=220 package=THT]
  R3 = Resistor [tolerance=±5% resistance=220 package=THT]
  IR-LED = LED - 5mm [color="Infrared (880nm)" package="5 mm [THT]"]
  LED_green_(MeasState) = LED - 5mm [color="Green (565nm)" package="5 mm [THT]"]
  R1 = Resistor [tolerance=±5% resistance=220 package=THT]
  IR-Transistor = LED - 5mm [color="Infrared (880nm)" package="5 mm [THT]"]

nets:
  N1: U1.D1, 0_96"_OLED.SCL
  N2: U1.D2, 0_96"_OLED.SDA
  3V3: U1.3V3, 0_96"_OLED.VCC
  GND: U1.GND, 0_96"_OLED.GND, R2.Pin_0, R3.Pin_0, LED_green_(MeasState).cathode
  N3: U1.D5, R1.Pin_0
  N4: U1.D6, IR-LED.anode
  N5: U1.RSV#40, IR-Transistor.anode
  N6: U1.A0, R2.Pin_1, IR-Transistor.cathode
  N7: R3.Pin_1, IR-LED.cathode
  N8: LED_green_(MeasState).anode, R1.Pin_1

custom parts:
  NodeMCU V1.0: ESP8266 based NodeMCU
